# Fritzing sketch button (saved by Fritzing 0.9.3b)
breadboards: 1

parts:
  A1 = Arduino UNO R4 WiFi
  S1 = Pushbutton [package="[THT]"]
  R1 = Resistor [tolerance=±5% resistance=220 package=THT]

nets:
  N1: A1.Pin_2, A1.Pin_48, R1.Pin_1
  N2: A1.Pin_8, S1.Pin_1, S1.Pin_2
  N3: A1.Pin_39, S1.Pin_3, S1.Pin_4, R1.Pin_0

custom parts:
  Arduino UNO R4 WiFi: The Arduino UNO R4 WiFi merges the RA4M1 microprocessor from Renesas with the ESP32-S3 from Espressif, creating an all-in-one tool for makers with enhanced processing power and a diverse array of new peripherals.
