# Fritzing sketch prelab1_circuitA (saved by Fritzing 0.9.3b)
breadboards: 1

parts:
  LED1 = LED - 5mm [color="Red (633nm)" package="5 mm [THT]"]
  R1 = Resistor [tolerance=±5% resistance=470 package=THT]
  A1 = Arduino UNO R4 WiFi

nets:
  N1: LED1.cathode, LED1.anode, A1.Pin_38
  N2: R1.Pin_1, A1.Pin_48

notes:
  long leg
  short leg

custom parts:
  Arduino UNO R4 WiFi: The Arduino UNO R4 WiFi merges the RA4M1 microprocessor from Renesas with the ESP32-S3 from Espressif, creating an all-in-one tool for makers with enhanced processing power and a diverse array of new peripherals.
